// Logisim project 9week.circ as structural Verilog
module S_R_Latch (
  input  Set,
  input  Reset,
  output Q,
  output Q_prime
);

  nor nor_1 (Q, Set, Q_prime);
  nor nor_2 (Q_prime, Q, Reset);
endmodule

module D_Latch (
  input  CLK,
  input  D,
  output Q,
  output Q_prime
);

  wire and_1_out, and_2_out, not_1_out;

  and and_1 (and_1_out, CLK, not_1_out);
  not not_1 (not_1_out, D);
  and and_2 (and_2_out, CLK, D);
  S_R_Latch S_R_Latch (.Set(and_1_out), .Reset(and_2_out), .Q(Q), .Q_prime(Q_prime));
endmodule

module D_FlipFlop (
  input  CLK,
  input  D,
  output Q
);

  wire d_latch_1_q, not_1_out;

  not not_1 (not_1_out, CLK);
  D_Latch d_latch_1 (.CLK(not_1_out), .D(D), .Q(d_latch_1_q));  // open: Q_prime
  D_Latch d_latch_2 (.CLK(CLK), .D(d_latch_1_q), .Q(Q));  // open: Q_prime
endmodule

module _4bitCounter (
  input  Reset,
  output [3:0] Output
);

  wire CLK_out;
  wire [3:0] adder_1_out;

  Adder #(.width(4)) adder_1 (.a(Output), .b(4'b0001), .out(adder_1_out));  // open: cin, cout
  Clock CLK (.out(CLK_out));
  Register #(.width(4)) Register (.D(adder_1_out), .Q(Output), .clk(CLK_out), .clr(Reset));  // open: en

  // Notes on the sheet:
  //   Adder
endmodule

module invertor (
  output Output,
  output Output_2
);

  wire CLK_2_out, CLK_out, not_1_out, not_2_out;

  Clock CLK (.out(CLK_out));
  D_FlipFlop d_flipflop_1 (.D(not_1_out), .CLK(CLK_out), .Q(Output));
  not not_1 (not_1_out, Output);
  Clock CLK_2 (.out(CLK_2_out));
  D_Flip_Flop d_ff_1 (.clk(CLK_2_out), .D(not_2_out), .Q(Output_2));  // open: Qn, preset, en, reset
  not not_2 (not_2_out, Output_2);
endmodule
