// Logisim project 10week.circ as structural Verilog
// 1Bit Adder
module _1bit_adder (
  input  A,
  input  B,
  input  Cin,
  output S,
  output Cout
);

  wire and_1_out, and_2_out, xor_1_out;

  xor xor_1 (xor_1_out, A, B);
  xor xor_2 (S, xor_1_out, Cin);
  and and_1 (and_1_out, Cin, xor_1_out);
  and and_2 (and_2_out, A, B);
  or or_1 (Cout, and_1_out, and_2_out);
endmodule

module _4bit_adder (
  input  A1,
  input  B1,
  input  A2,
  input  B2,
  input  A3,
  input  B3,
  input  A4,
  input  B4,
  output S1,
  output S2,
  output S3,
  output S4,
  output Cout
);

  wire n1bit_adder_1_cout, n1bit_adder_2_cout, n1bit_adder_3_cout;

  _1bit_adder u_1bit_adder_1 (.A(A1), .B(B1), .Cin(1'b0), .S(S1), .Cout(n1bit_adder_1_cout));
  _1bit_adder u_1bit_adder_2 (.A(A2), .B(B2), .Cin(n1bit_adder_1_cout), .S(S2), .Cout(n1bit_adder_2_cout));
  _1bit_adder u_1bit_adder_3 (.A(A3), .B(B3), .Cin(n1bit_adder_2_cout), .S(S3), .Cout(n1bit_adder_3_cout));
  _1bit_adder u_1bit_adder_4 (.A(A4), .B(B4), .Cin(n1bit_adder_3_cout), .S(S4), .Cout(Cout));
endmodule

module Moore (
  input  Ta,
  input  Tb,
  output LA1,
  output LA0,
  output LB1,
  output LB0
);

  wire and_1_out, and_2_out, clock_1_out, d_ff_2_q, not_1_out, not_2_out, not_3_out, not_4_out, or_1_out,
       xor_1_out;

  not not_1 (not_1_out, Ta);
  not not_2 (not_2_out, Tb);
  not not_3 (not_3_out, LA1);
  not not_4 (not_4_out, d_ff_2_q);
  xor xor_1 (xor_1_out, LA1, d_ff_2_q);
  and and_1 (and_1_out, not_1_out, not_3_out, not_4_out);
  and and_2 (and_2_out, not_4_out, LA1, not_2_out);
  Clock clock_1 (.out(clock_1_out));
  or or_1 (or_1_out, and_1_out, and_2_out);
  D_Flip_Flop d_ff_1 (.clk(clock_1_out), .D(xor_1_out), .Q(LA1));  // open: Qn, preset, en, reset
  D_Flip_Flop d_ff_2 (.clk(clock_1_out), .D(or_1_out), .Q(d_ff_2_q));  // open: Qn, preset, en, reset
  not not_5 (LB1, LA1);
  and and_3 (LA0, LB1, d_ff_2_q);
  and and_4 (LB0, LA1, d_ff_2_q);
endmodule

module _4bit_Adder_2 (
  input  [3:0] A,
  input  [3:0] B,
  output [3:0] S,
  output Overflow
);

  wire n1bit_adder_1_cout, n1bit_adder_2_cout, n1bit_adder_3_cout;

  _1bit_adder u_1bit_adder_1 (.A(A[0]), .B(B[0]), .Cin(1'b0), .S(S[0]), .Cout(n1bit_adder_1_cout));
  _1bit_adder u_1bit_adder_2 (.A(A[1]), .B(B[1]), .Cin(n1bit_adder_1_cout), .S(S[1]), .Cout(n1bit_adder_2_cout));
  _1bit_adder u_1bit_adder_3 (.A(A[2]), .B(B[2]), .Cin(n1bit_adder_2_cout), .S(S[2]), .Cout(n1bit_adder_3_cout));
  _1bit_adder u_1bit_adder_4 (.A(A[3]), .B(B[3]), .Cin(n1bit_adder_3_cout), .S(S[3]), .Cout(Overflow));
endmodule
