// Logisim project Week11.circ as structural Verilog
module _1bit_subtract (
  input  X,
  input  Y,
  input  Z,
  output D,
  output B
);

  wire and_1_out, and_2_out, not_1_out, not_2_out, xor_1_out;

  xor xor_1 (xor_1_out, X, Y);
  xor xor_2 (D, xor_1_out, Z);
  not not_1 (not_1_out, X);
  not not_2 (not_2_out, xor_1_out);
  and and_1 (and_1_out, not_1_out, Y);
  and and_2 (and_2_out, not_2_out, Z);
  or or_1 (B, and_1_out, and_2_out);
endmodule

module _4bit_subtract (
  input  [3:0] X,
  input  [3:0] Y,
  input  [3:0] X_2,
  input  [3:0] Y_2,
  output [3:0] D,
  output B,
  output [3:0] out_7
);

  wire n1bit_subtract_1_b, n1bit_subtract_2_b, n1bit_subtract_3_b;

  _1bit_subtract u_1bit_subtract_1 (.X(X[0]), .Y(Y[0]), .Z(1'b0), .D(D[0]), .B(n1bit_subtract_1_b));
  _1bit_subtract u_1bit_subtract_2 (.X(X[1]), .Y(Y[1]), .Z(n1bit_subtract_1_b), .D(D[1]), .B(n1bit_subtract_2_b));
  _1bit_subtract u_1bit_subtract_3 (.X(X[2]), .Y(Y[2]), .Z(n1bit_subtract_2_b), .D(D[2]), .B(n1bit_subtract_3_b));
  _1bit_subtract u_1bit_subtract_4 (.X(X[3]), .Y(Y[3]), .Z(n1bit_subtract_3_b), .D(D[3]), .B(B));
  Subtractor #(.width(4)) subtractor_1 (.a(X_2), .b(Y_2), .out(out_7));  // open: bin, bout
endmodule
