// Logisim project Week13.circ as structural Verilog
module _1bit_Adder (
  input  a,
  input  b,
  input  c_in,
  output sum,
  output c_out
);

  wire and_1_out, and_2_out, xor_1_out;

  xor xor_1 (xor_1_out, a, b);
  and and_1 (and_1_out, xor_1_out, c_in);
  and and_2 (and_2_out, a, b);
  xor xor_2 (sum, xor_1_out, c_in);
  or or_1 (c_out, and_1_out, and_2_out);
endmodule

module _4bit_Subtractor_using_1bit_Adder (
  input  [3:0] in_1,
  input  [3:0] in_2,
  output [3:0] D
);

  wire n1bit_adder_1_c_out, n1bit_adder_2_c_out, n1bit_adder_3_c_out;
  wire [3:0] not_1_out;

  assign not_1_out = ~in_2;  // NOT_Gate not_1, 4 bits wide
  _1bit_Adder u_1bit_adder_1 (.a(in_1[0]), .b(not_1_out[0]), .c_in(1'b1), .sum(D[0]), .c_out(n1bit_adder_1_c_out));
  _1bit_Adder u_1bit_adder_2 (
    .a(in_1[1]), .b(not_1_out[1]), .c_in(n1bit_adder_1_c_out), .sum(D[1]), .c_out(n1bit_adder_2_c_out));
  _1bit_Adder u_1bit_adder_3 (
    .a(in_1[2]), .b(not_1_out[2]), .c_in(n1bit_adder_2_c_out), .sum(D[2]), .c_out(n1bit_adder_3_c_out));
  _1bit_Adder u_1bit_adder_4 (.a(in_1[3]), .b(not_1_out[3]), .c_in(n1bit_adder_3_c_out), .sum(D[3]));  // open: c_out
endmodule

module _2_1_MUX (
  input  S,
  input  D0,
  input  D1,
  output Y
);

  wire and_1_out, and_2_out, not_1_out;

  not not_1 (not_1_out, S);
  and and_1 (and_1_out, not_1_out, D0);
  and and_2 (and_2_out, S, D1);
  or or_1 (Y, and_1_out, and_2_out);
endmodule

module _4_1_MUX (
  input  [1:0] S,
  input  D0,
  input  D1,
  input  D2,
  input  D3,
  output Y
);

  wire n2_1_mux_1_y, n2_1_mux_2_y;

  _2_1_MUX u_2_1_mux_1 (.S(S[0]), .D0(D0), .D1(D1), .Y(n2_1_mux_1_y));
  _2_1_MUX u_2_1_mux_2 (.S(S[0]), .D0(D2), .D1(D3), .Y(n2_1_mux_2_y));
  _2_1_MUX u_2_1_mux_3 (.S(S[1]), .D0(n2_1_mux_1_y), .D1(n2_1_mux_2_y), .Y(Y));
endmodule

module Right_Shifter (
  input  [1:0] Shift,
  input  [3:0] Input,
  output [3:0] Output
);

  _4_1_MUX u_4_1_mux_1 (.D0(Input[3]), .D1(1'b0), .D2(1'b0), .D3(1'b0), .S(Shift), .Y(Output[3]));
  _4_1_MUX u_4_1_mux_2 (.D0(Input[2]), .D1(Input[3]), .D2(1'b0), .D3(1'b0), .S(Shift), .Y(Output[2]));
  _4_1_MUX u_4_1_mux_3 (.D0(Input[1]), .D1(Input[2]), .D2(Input[3]), .D3(1'b0), .S(Shift), .Y(Output[1]));
  _4_1_MUX u_4_1_mux_4 (.D0(Input[0]), .D1(Input[1]), .D2(Input[2]), .D3(Input[3]), .S(Shift), .Y(Output[0]));
endmodule

module Left_Shifter (
  input  [1:0] Shift,
  input  [3:0] Input,
  output [3:0] Output
);

  _4_1_MUX u_4_1_mux_1 (.D0(Input[3]), .D1(Input[2]), .D2(Input[1]), .D3(Input[0]), .S(Shift), .Y(Output[3]));
  _4_1_MUX u_4_1_mux_2 (.D0(Input[2]), .D1(Input[1]), .D2(Input[0]), .D3(1'b0), .S(Shift), .Y(Output[2]));
  _4_1_MUX u_4_1_mux_3 (.D0(Input[1]), .D1(Input[0]), .D2(1'b0), .D3(1'b0), .S(Shift), .Y(Output[1]));
  _4_1_MUX u_4_1_mux_4 (.D0(Input[0]), .D1(1'b0), .D2(1'b0), .D3(1'b0), .S(Shift), .Y(Output[0]));
endmodule

module _3_5_Multiplier (
  input  [1:0] in_1,
  input  [3:0] X,
  output [3:0] Output
);

  wire [3:0] left_shifter_1_output, n4bit_adder_1_d, right_shifter_1_output;

  Left_Shifter left_shifter_1 (.Input(X), .Shift(in_1), .Output(left_shifter_1_output));
  Right_Shifter right_shifter_1 (.Input(X), .Shift(in_1), .Output(right_shifter_1_output));
  _4bit_Adder u_4bit_adder_1 (.in_1(left_shifter_1_output), .in_2(right_shifter_1_output), .D(n4bit_adder_1_d));
  _4bit_Adder u_4bit_adder_2 (.in_1(n4bit_adder_1_d), .in_2(X), .D(Output));
endmodule

module _4bit_Adder (
  input  [3:0] in_1,
  input  [3:0] in_2,
  output [3:0] D
);

  wire n1bit_adder_1_c_out, n1bit_adder_2_c_out, n1bit_adder_3_c_out;

  _1bit_Adder u_1bit_adder_1 (.a(in_1[0]), .b(in_2[0]), .c_in(1'b0), .sum(D[0]), .c_out(n1bit_adder_1_c_out));
  _1bit_Adder u_1bit_adder_2 (
    .a(in_1[1]), .b(in_2[1]), .c_in(n1bit_adder_1_c_out), .sum(D[1]), .c_out(n1bit_adder_2_c_out));
  _1bit_Adder u_1bit_adder_3 (
    .a(in_1[2]), .b(in_2[2]), .c_in(n1bit_adder_2_c_out), .sum(D[2]), .c_out(n1bit_adder_3_c_out));
  _1bit_Adder u_1bit_adder_4 (.a(in_1[3]), .b(in_2[3]), .c_in(n1bit_adder_3_c_out), .sum(D[3]));  // open: c_out
endmodule
